# Fritzing sketch OCB Conexoes (saved by Fritzing 0.9.3b)
circuit board: 7cm x 3cm
perfboards: 1

parts:
  Fones = Audio Jack (TRS) 3.5mm [package="4Ucon 08780 [THT]"]
  USB = USB Connectors [package=usb-a-pcb]
  DFRobot_DFPlayer_Mini1 = DFRobot DFPlayer Mini [part_number=DFR0299]
  J3 = female pin header, 2 pins [form="♀ (female)"]
  J1 = female pin header, 4 pins [form="♀ (female)"]
  J2 = female pin header, 5 pins [form="♀ (female)"]
  R1 = Resistor [tolerance=±5% resistance=330 package=THT]

nets:
  N1: Fones.Sleeve, USB.GND, DFRobot_DFPlayer_Mini1.GND-1, DFRobot_DFPlayer_Mini1.GND-2, J2.pin3
  N2: Fones.Ring, J2.pin1, J2.pin2
  N3: Fones.Tip, J2.pin4, J2.pin5
  N4: USB.VBUS, DFRobot_DFPlayer_Mini1.VCC
  N5: USB.D-, DFRobot_DFPlayer_Mini1.USB_NEG
  N6: USB.D+, DFRobot_DFPlayer_Mini1.USB_POS
  N7: DFRobot_DFPlayer_Mini1.RX, R1.Pin_0
  N8: DFRobot_DFPlayer_Mini1.TX, J1.pin2
  N9: DFRobot_DFPlayer_Mini1.SPK_1, J3.pin2
  N10: DFRobot_DFPlayer_Mini1.SPK_2, J3.pin1
  N11: DFRobot_DFPlayer_Mini1.BUSY, J1.pin1
  N12: J1.pin3, R1.Pin_1

custom parts:
  DFRobot DFPlayer Mini: The DFPlayer Mini is a small and low cost MP3 module with an simplified output directly to the speaker. The module can be used as a stand alone module with attached battery, speaker and push buttons or used in combination with an Arduino UNO or any other with RX/TX capabilities.
