# Fritzing sketch OCB Radio (saved by Fritzing 0.9.3b)
breadboards: 3

parts:
  Arduino_Mega_2560 = Arduino Mega 2560 (Rev3)
  RE1 = Rotary Encoder [package=THT]  # not connected
  S2 = Pushbutton [package="[THT]"]
  S3 = Pushbutton [package="[THT]"]
  U1 = POT_SWITCH [package=pot_pth_switch]  # not connected
  R1 = Resistor [tolerance=±5% resistance=10k package=THT]
  R4 = Resistor [tolerance=±5% resistance=10k package=THT]
  DFRobot_DFPlayer_Mini1 = DFRobot DFPlayer Mini [part_number=DFR0299]
  TRS1 = Audio Jack (TRS) 3.5mm [package="4Ucon 08780 [THT]"]
  S4 = Pushbutton [package="[THT]"]
  U3 = USB Connectors [package=usb-a-s-nosilk]
  U4 = 2-Channel 5v Relay Shield [package=relay-2ch5v10a]
  YwRobot_Power_Supply1 = YwRobot Breadboard Power Supply [part_number=545043]
  Power_plug1 = Power plug
  Componente1 = Digital FM Radio Receiver
  R6 = Resistor [tolerance=±5% resistance=10k package=THT]
  R5 = Resistor [tolerance=±5% resistance=10k package=THT]
  U6 = SD_CARD_SOCKET [package=sdcard_4uconn]
  J2 = screw terminal, 2 pins
  J1 = screw terminal, 2 pins
  R7 = Resistor [tolerance=±5% resistance=1k package=THT]
  R8 = Resistor [tolerance=±5% resistance=1k package=THT]
  U7 = mystery part, 10 pins [chip_label=OEP30WX2]
  Componente2 = Real Time Clock Module - DS1307 RTC Breakout Board

nets:
  N1: Arduino_Mega_2560.D21/SCL, Arduino_Mega_2560.SCL, Componente1.SCLK, Componente2.SCL
  N2: Arduino_Mega_2560.D20/SDA, Arduino_Mega_2560.SDA, Componente1.SDIO, Componente2.SDA
  N3: Arduino_Mega_2560.D17_PWM/RX2, R8.Pin_0
  N4: Arduino_Mega_2560.D16_PWM/TX2, R7.Pin_0
  N5: Arduino_Mega_2560.D9_PWM, S4.Pin_3, S4.Pin_4, R6.Pin_1
  N6: Arduino_Mega_2560.D8_PWM, R1.Pin_1
  N7: Arduino_Mega_2560.RESET, Componente1.!RST
  GND: Arduino_Mega_2560.GND, Power_plug1.GND, U7.pin6
  VIN: Arduino_Mega_2560.VIN, Power_plug1.VCC, U7.pin5
  N8: Arduino_Mega_2560.D3_PWM, DFRobot_DFPlayer_Mini1.BUSY
  N9: Arduino_Mega_2560.D4_PWM, U4.IN1
  N10: Arduino_Mega_2560.D5_PWM, U4.IN2
  N11: Arduino_Mega_2560.D6_PWM, S2.Pin_3, S2.Pin_4, R5.Pin_1
  N12: Arduino_Mega_2560.D7_PWM, S3.Pin_3, S3.Pin_4, R4.Pin_1
  N13: Arduino_Mega_2560.D50, U6.MISO
  N14: Arduino_Mega_2560.D51, U6.MOSI
  N15: Arduino_Mega_2560.D52, U6.CLK
  N16: Arduino_Mega_2560.D53, U6.CS
  VCC: S2.Pin_1, S2.Pin_2, S3.Pin_1, S3.Pin_2, R1.Pin_0, DFRobot_DFPlayer_Mini1.VCC, S4.Pin_1, S4.Pin_2, U3.VBUS, U4.VCC, YwRobot_Power_Supply1.VCC#5, YwRobot_Power_Supply1.VCC#6
  GND_2: R4.Pin_0, U3.GND, U4.GND, R6.Pin_0, R5.Pin_0
  N17: DFRobot_DFPlayer_Mini1.RX, R8.Pin_1
  N18: DFRobot_DFPlayer_Mini1.TX, R7.Pin_1
  N19: DFRobot_DFPlayer_Mini1.DAC_R, U4.K1-Off
  N20: DFRobot_DFPlayer_Mini1.DAC_L, U4.K2-Off
  N21: DFRobot_DFPlayer_Mini1.GND-1, DFRobot_DFPlayer_Mini1.GND-2
  N22: DFRobot_DFPlayer_Mini1.USB_POS, U3.D+
  N23: DFRobot_DFPlayer_Mini1.USB_NEG, U3.D-
  N24: TRS1.Sleeve, U7.pin8
  N25: TRS1.Ring, U4.K2-In, U7.pin9
  N26: TRS1.Tip, U4.K1-In, U7.pin7
  N27: YwRobot_Power_Supply1.VCC#9, YwRobot_Power_Supply1.VCC#10
  N28: YwRobot_Power_Supply1.GND#11, YwRobot_Power_Supply1.GND#12
  N29: YwRobot_Power_Supply1.GND#13, YwRobot_Power_Supply1.GND#14
  GND_3: Componente1.GND, U6.GND, Componente2.GND
  3.3V: Componente1.3.3V, U6.3v3, Componente2.5V
  N30: J2.pin1, U7.pin3
  N31: J2.pin2, U7.pin4
  N32: J1.pin1, U7.pin1
  N33: J1.pin2, U7.pin2

custom parts:
  DFRobot DFPlayer Mini: The DFPlayer Mini is a small and low cost MP3 module with an simplified output directly to the speaker. The module can be used as a stand alone module with attached battery, speaker and push buttons or used in combination with an Arduino UNO or any other with RX/TX capabilities.
  2-Channel 5v Relay Shield: 2 Channel 5v Relay Shield w. 2x SPD-06VDC-SD-C
  YwRobot Breadboard Power Supply: The YwRobot Breadboard Power Supply (MB-V2) has two power rails; they can be 5V or 3V3. Power to the module can be provided through the female USB socket or through the A10 (female) 2.1mm power jack.
  SD_CARD_SOCKET: SD Memory Card Connector, push-push normal type, CD enable, WP enable
